# Fritzing sketch bikeSense (saved by Fritzing 0.9.3b)

parts:
  BUTTON1 = Waterproof Pushbutton (green)
  Part3 = Adafruit Datalogger Shield v1 [part_number="Adafruit #1141"]
  SONAR1 = Maxbotix MaxSonar Ultrasonic Sensor (Hi-Res)
  S1 = SWITCH-SPST-2 [package=switch-spst-vertical]
  VCC1 = Battery
  VCC2 = Battery

nets:
  N1: BUTTON1.no_name_yet#1, Part3.D4
  N2: BUTTON1.no_name_yet#2, Part3.N$139, Part3.N$140, Part3.N$141, Part3.N$142, Part3.N$143, SONAR1.+5V
  N3: BUTTON1.no_name_yet#4, Part3.D3
  GND: BUTTON1.no_name_yet#5, Part3.GND, Part3.N$38, SONAR1.GND, VCC2.-
  N4: Part3.D2, SONAR1.PW
  N5: Part3.VIN, VCC1.+
  N6: Part3.+5V, Part3.N$138
  N7: S1.O, VCC1.-
  N8: S1.P, VCC2.+

custom parts:
  Waterproof Pushbutton (green): Waterproof Illuminated Pushbutton (green)
  Adafruit Datalogger Shield v1: Here's a handy Arduino shield: we've had a lot of people looking for a dedicated and well-designed data logging shield. We worked hard to engineer an inexpensive but well-rounded design. Not only is it easy to assemble and customize, it also comes with great documentation and libraries. New! we now are carrying an 'assembled' version of this shield, with all the components pre-soldered. NOTE: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
  Maxbotix MaxSonar Ultrasonic Sensor (Hi-Res): Maxbotix MaxSonar Hi-Resolution Ultrasonic Sensor HRLV-EZ0, HRLV-EZ1, HRLV-EZ2, HRLV-EZ3, HRLV-EZ4
